# Fritzing sketch radio-transmitter (saved by Fritzing 1.0.2b)
circuit board: 10cm x 10cm
breadboards: 1

parts:
  Componente1 = Arduino Nano (Rev3.0)
  Componente2 = NRF24L01+ Breakout Board
  LED1 = smd LED [color="Green (570nm)" package="1206 [SMD]"]
  R1 = Resistor [tolerance=±5% resistance=3300 package="0402 [SMD]"]
  BAT1 = BC9VPC [package=bc9vpc]
  S1 = Pushbutton [package="[SMD]"]
  S2 = Pushbutton [package="[SMD]"]
  S3 = Pushbutton [package="[SMD]"]
  S4 = Pushbutton [package="[SMD]"]
  S5 = Pushbutton [package="[SMD]"]
  S6 = Pushbutton [package="[SMD]"]

nets:
  GND: Componente1.GND, Componente2.GND, LED1.cathode, BAT1.V-, S1.Pin_3, S1.Pin_4, S2.Pin_3, S2.Pin_4, S3.Pin_3, S3.Pin_4, S4.Pin_3, S4.Pin_4, S5.Pin_1, S5.Pin_2, S6.Pin_1, S6.Pin_2
  N1: Componente1.D2, S2.Pin_1, S2.Pin_2
  N2: Componente1.D3, S1.Pin_1, S1.Pin_2
  N3: Componente1.D4, S4.Pin_1, S4.Pin_2
  N4: Componente1.D5, S3.Pin_1, S3.Pin_2
  N5: Componente1.D6, R1.Pin_0
  N6: Componente1.D7, Componente2.CS
  N7: Componente1.D8, Componente2.CE
  N8: Componente1.D11/MOSI, Componente2.MOSI
  N9: Componente1.D12/MISO, Componente2.MISO
  N10: Componente1.VIN, BAT1.V+
  N11: Componente1.A1, S6.Pin_3, S6.Pin_4
  N12: Componente1.A0, S5.Pin_3, S5.Pin_4
  3V3: Componente1.3V3, Componente2.VCC
  N13: Componente1.D13/SCK, Componente2.SCK
  N14: LED1.anode, R1.Pin_1

notes:
  D-PAD
  B-PAD
  upper
  lower
  left
  right
  3.3k

// code stored in the sketch: radio-transmitter.ino
#include <RF24.h>
#include <RF24_config.h>
#include <nRF24L01.h>
#include <printf.h>

#include "Pad.hpp"
#include "Throttle.hpp"

/*
    Radio transmitter 

    This sketch is the firware for a radio transmitter based on 
    transceiver module nRF24L01. The controller has 2 input pads,
    one with 4 push buttons, and the other with 2 push buttons,
    resulting in 6 digital inputs. All 6 inputs are treated as 
    channels and transmitted to the receiver independently. The 
    board used is an Arduino Nano.

    The circuit:
    - TODO 

    Created 10 April 2024 
    By Eduardo Vasconcelos 
    Modified 14 April 2024
    By Eduardo Vasconcelos

*/

// Directional pad 
Pad dPad = Pad(2, 3, 4, 5);

// Button pad 
Pad bPad = Pad(NULL, A0, NULL, A1);

// Indicator LED
uint8_t led = 6;

// Transmitter radio
RF24 radio(8, 7);
uint8_t address[6] = "wolf0";
int radioBuffer[6] = {
  -1, -1, -1, 
  -1, -1, -1
};

void setup() {
  // [begin] toggle comment for debugging
  Serial.begin(9600);
  // [end]

  // Indicator LED setup 
  pinMode(led, OUTPUT);
  digitalWrite(led, HIGH);

  // Radio setup 
  radio.begin();
  radio.openWritingPipe(address);
  radio.setPALevel(RF24_PA_HIGH);
  radio.stopListening();
}

void loop() {
  /*
      Transmission loop 

      1. Read all input states and store them in a 
      transmission buffer

      2. Transmit the buffer to the receiver
  */

  // Read controller state to radio buffer 
  readDPad();
  readBPad();

  // Transmit radio buffer to receiver 
  radio.write(&radioBuffer, sizeof(radioBuffer));

  // [begin] toggle comment for debugging
  logState();
  // This prevents flooding the serial monitor 
  // delay(1000);
  // [end]
}

void readDPad() {
  radioBuffer[0] = dPad.getUpper();
  radioBuffer[1] = dPad.getLeft();
  radioBuffer[2] = dPad.getLower();
  radioBuffer[3] = dPad.getRight();
}

void readBPad() {
  radioBuffer[4] = bPad.getLeft();
  radioBuffer[5] = bPad.getRight();
}

void logState() {
  Serial.println("=== Transmitter state ===");

  // dPad state
  Serial.println("\nDirectional pad:");
  Serial.print("- upper: ");
  Serial.println(dPad.getUpper());
  Serial.print("- left: ");
  Serial.println(dPad.getLeft());
  Serial.print("- lower: ");
  Serial.println(dPad.getLower());
  Serial.print("- right: ");
  Serial.println(dPad.getRight());

  // bPad state 
  Serial.println("\nButton pad:");
  Serial.print("- left: ");
  Serial.println(bPad.getLeft());
  Serial.print("- right: ");
  Serial.println(bPad.getRight());

  // Radio buffer 
  Serial.println("\nRadio buffer:");
  Serial.println("* READINGS MAY DIFFER TRANSITORILY FROM THE ONES ABOVE *");
  for (int i = 0; i < 6; i++) {
    Serial.print("- radioBuffer[");
    Serial.print(i);
    Serial.print("]: ");
    Serial.println(radioBuffer[i]);
  }

  Serial.println("========================");
}
